# Fritzing sketch Clapper-Fritzing (saved by Fritzing 0.8.3b)
circuit board: 16.9333cm x 5.64444cm
breadboards: 1

parts:
  IC1 = IC, DIP package, 14 pins [chip_label=ATtiny84]
  Part1 = Breakout Board for Electret Microphone
  LED2 = smd LED [color="White (4500K)" package="1206 [SMD]"]
  LED3 = smd LED [color="White (4500K)" package="1206 [SMD]"]
  LED4 = smd LED [color="Red (660nm)" package="1206 [SMD]"]
  R1 = Resistor [tolerance=±5% resistance=220 package="0603 [SMD]"]
  U1 = MOC3031-M [package=dil06]
  Triac_BTA08 = TRIAC [package=to-92]
  R3 = Resistor [tolerance=±5% resistance=1k package="0603 [SMD]"]
  R2 = Resistor [tolerance=±5% resistance=1k package="0805 [SMD]"]

nets:
  N1: IC1.pin1, Part1.AUD
  N2: IC1.pin6, LED3.anode
  N3: IC1.pin7, LED2.anode
  N4: IC1.pin8, R1.Pin_1, R2.Pin_0
  N5: IC1.pin13, Part1.GND
  N6: IC1.pin14, Part1.VCC, LED2.cathode, LED3.cathode, LED4.cathode
  N7: LED4.anode, R1.Pin_0
  N8: U1.1, Triac_BTA08.M2
  N9: U1.4, R2.Pin_1
  N10: Triac_BTA08.G, R3.Pin_1

notes:
  Power High
